# Fritzing sketch multiple_leds (saved by Fritzing 0.9.3b)
breadboards: 1

parts:
  Part1 = Arduino Uno (Rev3)
  R1 = Resistor [tolerance=±5% resistance=220 package=THT]
  R2 = Resistor [tolerance=±5% resistance=220 package=THT]
  R3 = Resistor [tolerance=±5% resistance=220 package=THT]
  R4 = Resistor [tolerance=±5% resistance=220 package=THT]
  R5 = Resistor [tolerance=±5% resistance=220 package=THT]
  R6 = Resistor [tolerance=±5% resistance=220 package=THT]
  R7 = Resistor [tolerance=±5% resistance=220 package=THT]
  R8 = Resistor [tolerance=±5% resistance=220 package=THT]
  LED1 = LED - 5mm [color="Red (633nm)" package="5 mm [THT]"]
  LED2 = LED - 5mm [color="Orange (620nm)" package="5 mm [THT]"]
  LED3 = LED - 5mm [color="Yellow (585nm)" package="5 mm [THT]"]
  LED4 = LED - 5mm [color="Green (565nm)" package="5 mm [THT]"]
  LED5 = LED - 5mm [color="Blue (430nm)" package="5 mm [THT]"]
  LED6 = LED - 5mm [color="Red (633nm)" package="5 mm [THT]"]
  LED7 = LED - 5mm [color="Orange (612nm)" package="5 mm [THT]"]
  LED8 = LED - 5mm [color="Yellow (585nm)" package="5 mm [THT]"]

nets:
  N1: Part1.D8, LED7.anode
  N2: Part1.D9_PWM, LED8.anode
  N3: Part1.D2, LED1.anode
  N4: Part1.D3_PWM, LED2.anode
  N5: Part1.D4, LED3.anode
  N6: Part1.D5_PWM, LED4.anode
  N7: Part1.D6_PWM, LED5.anode
  N8: Part1.D7, LED6.anode
  N9: Part1.GND, R2.Pin_0, R3.Pin_0, R4.Pin_0, R5.Pin_0, R6.Pin_0, R7.Pin_0, R8.Pin_0
  N10: R1.Pin_1, LED1.cathode
  N11: R2.Pin_1, LED2.cathode
  N12: R3.Pin_1, LED3.cathode
  N13: R4.Pin_1, LED4.cathode
  N14: R5.Pin_1, LED5.cathode
  N15: R6.Pin_1, LED6.cathode
  N16: R7.Pin_1, LED7.cathode
  N17: R8.Pin_1, LED8.cathode
