# Fritzing sketch photo_resistor (saved by Fritzing 0.9.3b)
breadboards: 1

parts:
  Part1 = Arduino Uno (Rev3)
  R1 = Resistor [tolerance=±5% resistance=220 package=THT]
  R2 = Resistor [tolerance=±5% resistance=10k package=THT]
  R3 = Photocell (LDR) [package=THT]  # not connected

nets:
  N1: Part1.A0, R2.Pin_0
  N2: Part1.GND, R1.Pin_1, R2.Pin_1
