# Fritzing sketch push_buttons (saved by Fritzing 0.9.3b)
breadboards: 1

parts:
  Part1 = Arduino Uno (Rev3)
  R1 = Resistor [tolerance=±5% resistance=220 package=THT]
  R2 = Resistor [tolerance=±5% resistance=10k package=THT]
  R3 = Resistor [tolerance=±5% resistance=10k package=THT]
  S1 = Pushbutton [package="[THT]"]
  S2 = Pushbutton [package="[THT]"]
  LED1 = LED - 5mm [color="Red (633nm)" package="5 mm [THT]"]

nets:
  N1: Part1.D13/SCK, LED1.anode
  N2: Part1.D2, R3.Pin_0, S1.Pin_1, S1.Pin_2
  N3: Part1.D3_PWM, R2.Pin_0, S2.Pin_1, S2.Pin_2
  N4: Part1.5V, R2.Pin_1, R3.Pin_1
  N5: Part1.GND, R1.Pin_1, S1.Pin_3, S1.Pin_4, S2.Pin_3, S2.Pin_4
  N6: R1.Pin_0, LED1.cathode
